# Fritzing sketch soil_measurement_sketch (saved by Fritzing 0.9.3b)
circuit board: 8.46667cm x 5.64444cm
breadboards: 1

parts:
  Bauteil1 = Arduino Nano (Rev3.0)
  U2 = FS1000A - 433Mhz RF Transmitter [package=THT]
  U3 = XD-RF-5V [package=THT]
  LED1 = LED - 5mm [color="Green (570nm)" package="5 mm [THT]"]
  C1 = Electrolytic Capacitor [capacitance=10µF voltage=50V package="100 mil [THT, electrolytic]"]
  C3 = Ceramic Capacitor [capacitance=100nF voltage=16V package="100 mil [THT, multilayer]"]
  C4 = Ceramic Capacitor [capacitance=100nF voltage=16V package="100 mil [THT, multilayer]"]
  ANT1 = Antenna
  ANT2 = Antenna
  LED2 = LED - 5mm [color="Green (570nm)" package="5 mm [THT]"]
  R2 = Resistor [tolerance=±2% resistance=220 package=THT]
  R3 = Resistor [tolerance=±2% resistance=220 package=THT]
  C5 = Electrolytic Capacitor [capacitance=10µF voltage=50V package="100 mil [THT, electrolytic]"]
  LED3 = LED - 5mm [color="Red (635nm)" package="5 mm [THT]"]
  U4 = attiny85 [package=dip]
  R1 = Resistor [tolerance=±2% resistance=220 package=THT]
  J1 = Piezo Speaker

nets:
  GND: Bauteil1.GND, U2.GND, U3.GND, C1.-, C1.+, C3.0, C3.1, U4.Pin_4, R1.Pin_0, J1.pin2
  N1: Bauteil1.D4, LED1.anode
  N2: Bauteil1.D11/MOSI, U3.DATA#2
  VCC: Bauteil1.5V, U2.VCC, U3.VCC, C4.0, C4.1, C5.-, C5.+, U4.Pin_8
  N3: U2.DATA, U4.Pin_3
  N4: U2.Antenna, ANT1.antenna_lead
  N5: U3.Attenna, ANT2.antenna_lead
  N6: LED1.cathode, R1.Pin_1
  N7: LED2.cathode, R3.Pin_0
  N8: LED2.anode, U4.Pin_7
  N9: R2.Pin_0, LED3.cathode
  N10: R2.Pin_1, R3.Pin_1
  N11: LED3.anode, U4.Pin_6
  N12: U4.Pin_5, J1.pin1

custom parts:
  FS1000A - 433Mhz RF Transmitter: This is 433Mhz RF transmitter with receiver kit for Arduino ARM MCU wireless Application environment: Remote control switch, receiver module, motorcycles, automobile anti-theft products, home security products, electric doors, shutter doors, windows, remote control socket, remote control LED, remote audio remote control electric doors, garage door remote control, remote control retractable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
  XD-RF-5V: This is 433Mhz RF transmitter with receiver kit for Arduino ARM MCU wireless Application environment: Remote control switch, receiver module, motorcycles, automobile anti-theft products, home security products, electric doors, shutter doors, windows, remote control socket, remote control LED, remote audio remote control electric doors, garage door remote control, remote control retractable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
