# Fritzing sketch soil_measurement_sketch_v3 (saved by Fritzing 0.9.3b)
breadboards: 1

parts:
  U1 = FS1000A - 433Mhz RF Transmitter [package=THT]
  U2 = XD-RF-5V [package=THT]  # not connected
  U3 = attiny85 [package=dip]
  BAT1 = Battery Holders [package=battcon_245mm_pth]
  C1 = Ceramic Capacitor [capacitance=100nF package="100 mil [THT, multilayer]"]
  C2 = Ceramic Capacitor [capacitance=100nF package="100 mil [THT, multilayer]"]
  C3 = Electrolytic Capacitor [capacitance=1µF package="100 mil [THT, electrolytic]"]
  C4 = Electrolytic Capacitor [capacitance=1µF package="100 mil [THT, electrolytic]"]
  R1 = Resistor [tolerance=±2% resistance=1k package=THT]
  R2 = Resistor [tolerance=±2% resistance=1k package=THT]
  SG1 = Buzzer 12mm [package=buzzer-12mm-ns]
  Q1 = NPN-Transistor [package="TO92 [THT]"]

nets:
  N1: U1.DATA, U3.Pin_2
  N2: U1.VCC, BAT1.+, C1.1, C3.-, SG1.1, Q1.E
  N3: U1.GND, BAT1.-, C2.0, C4.-
  N4: U3.Pin_4, C2.1, C4.+
  N5: U3.Pin_6, R1.Pin_0
  N6: U3.Pin_8, C1.0, C3.+
  N7: R1.Pin_1, Q1.B
  N8: R2.Pin_0, Q1.C
  N9: R2.Pin_1, SG1.2

custom parts:
  FS1000A - 433Mhz RF Transmitter: This is 433Mhz RF transmitter with receiver kit for Arduino ARM MCU wireless Application environment: Remote control switch, receiver module, motorcycles, automobile anti-theft products, home security products, electric doors, shutter doors, windows, remote control socket, remote control LED, remote audio remote control electric doors, garage door remote control, remote control retractable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
  XD-RF-5V: This is 433Mhz RF transmitter with receiver kit for Arduino ARM MCU wireless Application environment: Remote control switch, receiver module, motorcycles, automobile anti-theft products, home security products, electric doors, shutter doors, windows, remote control socket, remote control LED, remote audio remote control electric doors, garage door remote control, remote control retractable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
