# Fritzing sketch soil_measurement_sketch_v4_coin_adjusted (saved by Fritzing 0.9.3b)
breadboards: 1

parts:
  U1 = FS1000A - 433Mhz RF Transmitter [package=THT]
  U2 = XD-RF-5V [package=THT]  # not connected
  U3 = attiny85 [package=dip]
  BAT1 = Battery Holders [package=battcon_245mm_pth]
  C1 = Ceramic Capacitor [capacitance=100nF package="100 mil [THT, multilayer]"]
  C2 = Ceramic Capacitor [capacitance=100nF package="100 mil [THT, multilayer]"]
  C3 = Electrolytic Capacitor [capacitance=1µF package="100 mil [THT, electrolytic]"]
  C4 = Electrolytic Capacitor [capacitance=1µF package="100 mil [THT, electrolytic]"]
  R1 = Resistor [tolerance=±2% resistance=1k package=THT]
  R2 = Resistor [tolerance=±2% resistance=1k package=THT]
  SG1 = Buzzer 12mm [package=buzzer-12mm-ns]
  Q1 = NPN-Transistor [package="TO92 [THT]"]
  S1 = Momentary Switch [package=ksa_sealed_tac_switch]
  R3 = Resistor [tolerance=±2% resistance=1k package=THT]
  U4 = SWITCH_SPDT [package=kps-1290]

nets:
  N1: U1.DATA, U3.Pin_2
  N2: U1.VCC, C1.1, C3.-, SG1.1, Q1.E, R3.Pin_0, U4.P
  N3: U1.GND, BAT1.-, C2.0, C4.-, S1.2
  N4: U3.Pin_4, C2.1, C4.+
  N5: U3.Pin_6, R1.Pin_0
  N6: U3.Pin_7, S1.3, R3.Pin_1
  N7: U3.Pin_8, C1.0, C3.+
  N8: BAT1.+, U4.O
  N9: R1.Pin_1, Q1.B
  N10: R2.Pin_0, Q1.C
  N11: R2.Pin_1, SG1.2

custom parts:
  FS1000A - 433Mhz RF Transmitter: This is 433Mhz RF transmitter with receiver kit for Arduino ARM MCU wireless Application environment: Remote control switch, receiver module, motorcycles, automobile anti-theft products, home security products, electric doors, shutter doors, windows, remote control socket, remote control LED, remote audio remote control electric doors, garage door remote control, remote control retractable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
  XD-RF-5V: This is 433Mhz RF transmitter with receiver kit for Arduino ARM MCU wireless Application environment: Remote control switch, receiver module, motorcycles, automobile anti-theft products, home security products, electric doors, shutter doors, windows, remote control socket, remote control LED, remote audio remote control electric doors, garage door remote control, remote control retractable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
